// Logisim project tictactoe.circ as structural Verilog: 4 circuits, main circuit main
module main (
  input  in_1,
  input  [3:0] in_2,
  input  [1:0] in_3
);

  wire button_1_out, button_2_out, button_3_out, button_4_out, button_5_out, button_6_out, button_7_out,
       button_8_out, button_9_out, button_press_capture_1_out_7, button_press_capture_1_out_8;
  wire [1:0] symbol_display_router_1_h0, symbol_display_router_1_h1, symbol_display_router_1_h2,
       symbol_display_router_1_v0, symbol_display_router_1_v1, symbol_display_router_1_v2;
  wire [2:2] tic_tac_toe_cell_1_hout, tic_tac_toe_cell_1_vout, tic_tac_toe_cell_2_hout,
       tic_tac_toe_cell_3_hout, tic_tac_toe_cell_4_vout, tic_tac_toe_cell_7_vout;
  wire [3:0] button_press_capture_1_out_9, tic_tac_toe_cell_1_l0, tic_tac_toe_cell_1_l1,
       tic_tac_toe_cell_1_l2, tic_tac_toe_cell_1_l3, tic_tac_toe_cell_2_l0, tic_tac_toe_cell_2_l1,
       tic_tac_toe_cell_2_l2, tic_tac_toe_cell_2_l3, tic_tac_toe_cell_3_l0, tic_tac_toe_cell_3_l1,
       tic_tac_toe_cell_3_l2, tic_tac_toe_cell_3_l3, tic_tac_toe_cell_4_l0, tic_tac_toe_cell_4_l1,
       tic_tac_toe_cell_4_l2, tic_tac_toe_cell_4_l3, tic_tac_toe_cell_5_l0, tic_tac_toe_cell_5_l1,
       tic_tac_toe_cell_5_l2, tic_tac_toe_cell_5_l3, tic_tac_toe_cell_6_l0, tic_tac_toe_cell_6_l1,
       tic_tac_toe_cell_6_l2, tic_tac_toe_cell_6_l3, tic_tac_toe_cell_7_l0, tic_tac_toe_cell_7_l1,
       tic_tac_toe_cell_7_l2, tic_tac_toe_cell_7_l3, tic_tac_toe_cell_8_l0, tic_tac_toe_cell_8_l1,
       tic_tac_toe_cell_8_l2, tic_tac_toe_cell_8_l3, tic_tac_toe_cell_9_l0, tic_tac_toe_cell_9_l1,
       tic_tac_toe_cell_9_l2, tic_tac_toe_cell_9_l3;

  Symbol_Display_Router symbol_display_router_1 (
    .clock(in_1), .XY(in_2), .SymID(in_3), .H0(symbol_display_router_1_h0), .H1(symbol_display_router_1_h1),
    .H2(symbol_display_router_1_h2), .V0(symbol_display_router_1_v0), .V1(symbol_display_router_1_v1),
    .V2(symbol_display_router_1_v2));
  Tic_Tac_Toe_Cell tic_tac_toe_cell_1 (
    .hin(symbol_display_router_1_h0), .vin(symbol_display_router_1_v0), .button(button_1_out),
    .hout(tic_tac_toe_cell_1_hout[2]), .L0(tic_tac_toe_cell_1_l0), .L1(tic_tac_toe_cell_1_l1),
    .L2(tic_tac_toe_cell_1_l2), .L3(tic_tac_toe_cell_1_l3), .vout(tic_tac_toe_cell_1_vout[2]));
  DotMatrix #(.inputtype("row"), .matrixcols(4), .matrixrows(4)) dotmatrix_1 (
    .row0(tic_tac_toe_cell_1_l0), .row1(tic_tac_toe_cell_1_l1), .row2(tic_tac_toe_cell_1_l2),
    .row3(tic_tac_toe_cell_1_l3));
  Button button_1 (.out(button_1_out));
  DotMatrix #(.inputtype("row"), .matrixcols(4), .matrixrows(4)) dotmatrix_2 (
    .row0(tic_tac_toe_cell_2_l0), .row1(tic_tac_toe_cell_2_l1), .row2(tic_tac_toe_cell_2_l2),
    .row3(tic_tac_toe_cell_2_l3));
  Tic_Tac_Toe_Cell tic_tac_toe_cell_2 (
    .hin(symbol_display_router_1_h1), .vin(symbol_display_router_1_v0), .button(button_2_out),
    .hout(tic_tac_toe_cell_2_hout[2]), .L0(tic_tac_toe_cell_2_l0), .L1(tic_tac_toe_cell_2_l1),
    .L2(tic_tac_toe_cell_2_l2), .L3(tic_tac_toe_cell_2_l3), .vout(tic_tac_toe_cell_1_vout[2]));
  Button button_2 (.out(button_2_out));
  DotMatrix #(.inputtype("row"), .matrixcols(4), .matrixrows(4)) dotmatrix_3 (
    .row0(tic_tac_toe_cell_3_l0), .row1(tic_tac_toe_cell_3_l1), .row2(tic_tac_toe_cell_3_l2),
    .row3(tic_tac_toe_cell_3_l3));
  Tic_Tac_Toe_Cell tic_tac_toe_cell_3 (
    .hin(symbol_display_router_1_h2), .vin(symbol_display_router_1_v0), .button(button_3_out),
    .hout(tic_tac_toe_cell_3_hout[2]), .L0(tic_tac_toe_cell_3_l0), .L1(tic_tac_toe_cell_3_l1),
    .L2(tic_tac_toe_cell_3_l2), .L3(tic_tac_toe_cell_3_l3), .vout(tic_tac_toe_cell_1_vout[2]));
  Button button_3 (.out(button_3_out));
  Tic_Tac_Toe_Cell tic_tac_toe_cell_4 (
    .hin(symbol_display_router_1_h0), .vin(symbol_display_router_1_v1), .button(button_4_out),
    .hout(tic_tac_toe_cell_1_hout[2]), .L0(tic_tac_toe_cell_4_l0), .L1(tic_tac_toe_cell_4_l1),
    .L2(tic_tac_toe_cell_4_l2), .L3(tic_tac_toe_cell_4_l3), .vout(tic_tac_toe_cell_4_vout[2]));
  DotMatrix #(.inputtype("row"), .matrixcols(4), .matrixrows(4)) dotmatrix_4 (
    .row0(tic_tac_toe_cell_4_l0), .row1(tic_tac_toe_cell_4_l1), .row2(tic_tac_toe_cell_4_l2),
    .row3(tic_tac_toe_cell_4_l3));
  DotMatrix #(.inputtype("row"), .matrixcols(4), .matrixrows(4)) dotmatrix_5 (
    .row0(tic_tac_toe_cell_5_l0), .row1(tic_tac_toe_cell_5_l1), .row2(tic_tac_toe_cell_5_l2),
    .row3(tic_tac_toe_cell_5_l3));
  Tic_Tac_Toe_Cell tic_tac_toe_cell_5 (
    .hin(symbol_display_router_1_h1), .vin(symbol_display_router_1_v1), .button(button_5_out),
    .hout(tic_tac_toe_cell_2_hout[2]), .L0(tic_tac_toe_cell_5_l0), .L1(tic_tac_toe_cell_5_l1),
    .L2(tic_tac_toe_cell_5_l2), .L3(tic_tac_toe_cell_5_l3), .vout(tic_tac_toe_cell_4_vout[2]));
  Tic_Tac_Toe_Cell tic_tac_toe_cell_6 (
    .hin(symbol_display_router_1_h2), .vin(symbol_display_router_1_v1), .button(button_6_out),
    .hout(tic_tac_toe_cell_3_hout[2]), .L0(tic_tac_toe_cell_6_l0), .L1(tic_tac_toe_cell_6_l1),
    .L2(tic_tac_toe_cell_6_l2), .L3(tic_tac_toe_cell_6_l3), .vout(tic_tac_toe_cell_4_vout[2]));
  DotMatrix #(.inputtype("row"), .matrixcols(4), .matrixrows(4)) dotmatrix_6 (
    .row0(tic_tac_toe_cell_6_l0), .row1(tic_tac_toe_cell_6_l1), .row2(tic_tac_toe_cell_6_l2),
    .row3(tic_tac_toe_cell_6_l3));
  Button button_4 (.out(button_4_out));
  Button button_5 (.out(button_5_out));
  Button button_6 (.out(button_6_out));
  DotMatrix #(.inputtype("row"), .matrixcols(4), .matrixrows(4)) dotmatrix_7 (
    .row0(tic_tac_toe_cell_7_l0), .row1(tic_tac_toe_cell_7_l1), .row2(tic_tac_toe_cell_7_l2),
    .row3(tic_tac_toe_cell_7_l3));
  Tic_Tac_Toe_Cell tic_tac_toe_cell_7 (
    .hin(symbol_display_router_1_h0), .vin(symbol_display_router_1_v2), .button(button_7_out),
    .hout(tic_tac_toe_cell_1_hout[2]), .L0(tic_tac_toe_cell_7_l0), .L1(tic_tac_toe_cell_7_l1),
    .L2(tic_tac_toe_cell_7_l2), .L3(tic_tac_toe_cell_7_l3), .vout(tic_tac_toe_cell_7_vout[2]));
  Button button_7 (.out(button_7_out));
  DotMatrix #(.inputtype("row"), .matrixcols(4), .matrixrows(4)) dotmatrix_8 (
    .row0(tic_tac_toe_cell_8_l0), .row1(tic_tac_toe_cell_8_l1), .row2(tic_tac_toe_cell_8_l2),
    .row3(tic_tac_toe_cell_8_l3));
  Tic_Tac_Toe_Cell tic_tac_toe_cell_8 (
    .hin(symbol_display_router_1_h1), .vin(symbol_display_router_1_v2), .button(button_8_out),
    .hout(tic_tac_toe_cell_2_hout[2]), .L0(tic_tac_toe_cell_8_l0), .L1(tic_tac_toe_cell_8_l1),
    .L2(tic_tac_toe_cell_8_l2), .L3(tic_tac_toe_cell_8_l3), .vout(tic_tac_toe_cell_7_vout[2]));
  Button button_8 (.out(button_8_out));
  DotMatrix #(.inputtype("row"), .matrixcols(4), .matrixrows(4)) dotmatrix_9 (
    .row0(tic_tac_toe_cell_9_l0), .row1(tic_tac_toe_cell_9_l1), .row2(tic_tac_toe_cell_9_l2),
    .row3(tic_tac_toe_cell_9_l3));
  Tic_Tac_Toe_Cell tic_tac_toe_cell_9 (
    .hin(symbol_display_router_1_h2), .vin(symbol_display_router_1_v2), .button(button_9_out),
    .hout(tic_tac_toe_cell_3_hout[2]), .L0(tic_tac_toe_cell_9_l0), .L1(tic_tac_toe_cell_9_l1),
    .L2(tic_tac_toe_cell_9_l2), .L3(tic_tac_toe_cell_9_l3), .vout(tic_tac_toe_cell_7_vout[2]));
  Button button_9 (.out(button_9_out));
  Button_Press_Capture button_press_capture_1 (
    .in_3(tic_tac_toe_cell_3_hout[2]), .out_9(button_press_capture_1_out_9),
    .in_2(tic_tac_toe_cell_2_hout[2]), .in_1(tic_tac_toe_cell_1_hout[2]), .in_6(tic_tac_toe_cell_7_vout[2]),
    .in_4(tic_tac_toe_cell_4_vout[2]), .in_5(tic_tac_toe_cell_1_vout[2]),
    .out_7(button_press_capture_1_out_7), .out_8(button_press_capture_1_out_8));

  // Notes on the sheet:
  //   TO DO
endmodule

module Tic_Tac_Toe_Cell (
  input  [1:0] hin,
  input  [1:0] vin,
  input  button,
  output [3:0] L0,
  output [3:0] L1,
  output [3:0] L2,
  output [3:0] L3,
  output hout,
  output vout
);

  wire and_1_out;
  wire [1:0] sym_req_q;

  Transistor #(.\type ("n")) transistor_1 (.in(1'b0), .out(hout), .gate(button));
  and and_1 (and_1_out, hin[1], vin[1]);
  Register #(.width(2)) sym_req (.D({vin[0], hin[0]}), .en(and_1_out), .Q(sym_req_q), .clk(and_1_out));  // open: clr
  ROM #(.addrWidth(2), .dataWidth(16)) rom_1 (.addr(sym_req_q), .data({L3, L2, L1, L0}));  // open: sel

  assign vout = hout;

  // Notes on the sheet:
  //   symID
  //   addr
  //   symbols
  //   bitmap
  //   contents of rom_1 (hex, n*v repeats v):
  //   0 9429 f99f 1234
endmodule

module Button_Press_Capture (
  input  in_1,
  input  in_2,
  input  in_3,
  input  in_4,
  input  in_5,
  input  in_6,
  output out_7,
  output out_8,
  output [3:0] out_9
);
endmodule

module Symbol_Display_Router (
  input  [1:0] SymID,
  input  clock,
  input  [3:0] XY,
  output [1:0] H0,
  output [1:0] H1,
  output [1:0] H2,
  output [1:0] V0,
  output [1:0] V1,
  output [1:0] V2
);

  wire and_1_out, and_2_out, and_3_out, and_4_out, and_5_out, and_6_out;

  and and_1 (and_1_out, ~XY[0], ~XY[1]);  // AND_Gate
  and and_2 (and_2_out, XY[0], ~XY[1]);  // AND_Gate
  and and_3 (and_3_out, ~XY[0], XY[1]);  // AND_Gate
  and and_4 (and_4_out, ~XY[2], ~XY[3]);  // AND_Gate
  and and_5 (and_5_out, XY[2], ~XY[3]);  // AND_Gate
  and and_6 (and_6_out, ~XY[2], XY[3]);  // AND_Gate
  Multiplexer #(.width(2), .enable("false")) multiplexer_1 (
    .in1({clock, SymID[0]}), .out(H0), .sel(and_1_out));  // open: in0
  Multiplexer #(.width(2), .enable("false")) multiplexer_2 (
    .in1({clock, SymID[0]}), .out(H1), .sel(and_2_out));  // open: in0
  Multiplexer #(.width(2), .enable("false")) multiplexer_3 (
    .in1({clock, SymID[0]}), .out(H2), .sel(and_3_out));  // open: in0
  Multiplexer #(.width(2), .enable("false")) multiplexer_4 (
    .in1({clock, SymID[1]}), .out(V0), .sel(and_4_out));  // open: in0
  Multiplexer #(.width(2), .enable("false")) multiplexer_5 (
    .in1({clock, SymID[1]}), .out(V1), .sel(and_5_out));  // open: in0
  Multiplexer #(.width(2), .enable("false")) multiplexer_6 (
    .in1({clock, SymID[1]}), .out(V2), .sel(and_6_out));  // open: in0

  // Other names for the same wires on the sheet: Htrue[1:0] = {clock, SymID[0]}; Vtrue[1:0] = {clock, SymID[1]}

  // Notes on the sheet:
  //   xcoord
  //   ycoord
endmodule
